# Fritzing sketch ArduinoOpenLog (saved by Fritzing 0.7.7b)
breadboards: 1

parts:
  Part1 = Arduino Pro Mini 3.3V  # not connected
  U1 = Voltage Regulator - 5V [package="TO220 [THT]"]
  VCC1 = Battery block 9V

nets:
  N1: U1.input_voltage, VCC1.+
  N2: U1.GND, VCC1.-
